# Fritzing sketch LCD wire up (saved by Fritzing 0.9.3b)
circuit board: 12.8379cm x 9.52198cm
breadboards: 1

parts:
  Part1 = Arduino Uno (Rev3)
  R1 = Resistor [tolerance=±5% resistance=10k package=THT]
  R2 = Resistor [tolerance=±5% resistance=10k package=THT]
  R3 = Resistor [tolerance=±5% resistance=10k package=THT]
  R7 = Resistor [tolerance=±5% resistance=10k package=THT]
  LCD1 = LCD_2.8_TFT_SPI_240X320_V1 [package=2.8]
  R10 = Resistor [tolerance=±5% resistance=10k package=THT]
  R11 = Resistor [tolerance=±5% resistance=10k package=THT]
  R12 = Resistor [tolerance=±5% resistance=10k package=THT]

nets:
  N1: Part1.D8, R2.Pin_1
  N2: Part1.D9_PWM, R3.Pin_1
  N3: Part1.D10_PWM/SS, R1.Pin_1
  N4: Part1.D11_PWM/MOSI, R11.Pin_1
  N5: Part1.D12/MISO, LCD1.SDO(MISO), LCD1.T_DO, LCD1.SD_MISO
  N6: Part1.D13/SCK, R10.Pin_1
  N7: Part1.D6_PWM, R12.Pin_1
  N8: Part1.D7, R7.Pin_1
  5V: Part1.5V, LCD1.VCC, LCD1.LED
  GND: Part1.GND, LCD1.GND
  N9: R1.Pin_0, LCD1.CS
  N10: R2.Pin_0, LCD1.RESET
  N11: R3.Pin_0, LCD1.DC
  N12: R7.Pin_0, LCD1.T_CS
  N13: LCD1.SDI(MOSI), LCD1.T_DIN, LCD1.SD_MOSI, R11.Pin_0
  N14: LCD1.SCK, LCD1.T_CLK, LCD1.SD_SCK, R10.Pin_0
  N15: LCD1.SD_CS, R12.Pin_0

notes:
  CLK
  MISO
  MOSI
  T_CS
  LCD_CS
  SD_CS
  LCD_RESET
  LCD_DC

custom parts:
  LCD_2.8_TFT_SPI_240X320_V1: LCD_2.8_TFT_SPI_240X320_V1 with sdcard and touch screen
