# Fritzing sketch Project (saved by Fritzing 0.9.3b)
breadboards: 2

parts:
  Part1 = Arduino Mega ADK (Rev3)
  BAT1 = BC9VPC [package=bc9vpc]
  R1 = Resistor [tolerance=±5% resistance=220 package=THT]
  R2 = Resistor [tolerance=±5% resistance=220 package=THT]
  M1 = DC Motor  # not connected
  KY-1 = TONGLING Relay [package=THT]
  KY-2 = TONGLING Relay [package=THT]
  S1 = Momentary Switch [package=ksa_sealed_tac_switch]
  S2 = Momentary Switch [package=ksa_sealed_tac_switch]
  R3 = Resistor [tolerance=±5% resistance=220 package=THT]
  R4 = Resistor [tolerance=±5% resistance=220 package=THT]
  L1 = Solenoid
  KY-3 = TONGLING Relay [package=THT]
  L2 = Solenoid
  R5 = Resistor [tolerance=±5% resistance=220 package=THT]

nets:
  N1: Part1.A1, R1.Pin_1, R2.Pin_1
  N2: Part1.D15/RX3, S1.1, S1.2, R3.Pin_0
  N3: Part1.D14/TX3, S2.1, S2.2, R4.Pin_0
  GND: Part1.GND, KY-1.GND, KY-2.GND, R3.Pin_1, R4.Pin_1, KY-3.GND
  N4: Part1.D9_PWM, KY-3.IN
  N5: Part1.D8_PWM, KY-2.IN
  VCC: Part1.5V, KY-1.VCC, KY-2.VCC, S1.3, S1.4, S2.3, S2.4, KY-3.VCC
  N6: Part1.D6_PWM, KY-1.IN
  N7: BAT1.V+, R2.Pin_0, KY-1.NO, KY-2.NO, KY-3.NO
  N8: BAT1.V-, R1.Pin_0, L1.pin1, L2.pin1, R5.Pin_0, R5.Pin_1
  N9: KY-2.C, L1.pin2
  N10: KY-3.C, L2.pin2

custom parts:
  TONGLING Relay: The TONGLING 5V relay module is suitable for SCM development, home appliance control. It uses a 5V~12V TIL control signal which can control DC / AC signal.
