# Fritzing sketch פריצינג סופי של הפרוייקט (saved by Fritzing 0.9.4)
breadboards: 3

parts:
  Part1 = Arduino Mega ADK (Rev3)
  U1 = ESP8266 WiFi Module [part_number=ESP8266]
  KY-1 = TONGLING Relay [package=THT]
  KY-2 = TONGLING Relay [package=THT]
  KY-3 = TONGLING Relay [package=THT]
  KY-4 = TONGLING Relay [package=THT]
  F1 = FUSE [package=fuse_5mm]
  R1 = Resistor [tolerance=±5% resistance=21k package=THT]
  D1 = Rectifier Diode [part_number=1N4001 package="300 mil [THT]"]
  J2 = Screw terminal - 2 pins [package=THT]
  R3 = Resistor [tolerance=±5% resistance=15k package=THT]
  R4 = Resistor [tolerance=±5% resistance=8.2k package=THT]
  J3 = Screw terminal - 2 pins [package=THT]
  J4 = Screw terminal - 2 pins [package=THT]
  J5 = Screw terminal - 2 pins [package=THT]
  D2 = Rectifier Diode [part_number=1N4001 package="300 mil [THT]"]
  D3 = Rectifier Diode [part_number=1N4001 package="300 mil [THT]"]
  J6 = Screw terminal - 2 pins [package=THT]
  R5 = Resistor [tolerance=±5% resistance=8.2k package=THT]
  R6 = Resistor [tolerance=±5% resistance=15k package=THT]
  R7 = Resistor [tolerance=±5% resistance=8.2k package=THT]
  R8 = Resistor [tolerance=±5% resistance=15k package=THT]
  S1 = Pushbutton [package="[THT]"]
  S2 = Pushbutton [package="[THT]"]
  R9 = Resistor [tolerance=±5% resistance=10k package=THT]
  R10 = Resistor [tolerance=±5% resistance=10k package=THT]
  Tiny_RTC1 = Tiny RTC
  Mod1 = KY-015 Temperature & Humidity Sensor Module [package="Breakout board"]
  Mod2 = KY-015 Temperature & Humidity Sensor Module [package="Breakout board"]
  Mod3 = KY-015 Temperature & Humidity Sensor Module [package="Breakout board"]
  R11 = Resistor [tolerance=±5% resistance=220 package=THT]
  R12 = Photocell (LDR) [package=THT]
  R13 = Photocell (LDR) [package=THT]
  R14 = Photocell (LDR) [package=THT]
  R15 = Resistor [tolerance=±5% resistance=220 package=THT]
  R16 = Resistor [tolerance=±5% resistance=220 package=THT]
  Part2 = Turbidity driver sensor
  LCD1 = LCD_2.8_TFT_SPI_240X320_V1 [package=2.8]
  BAT2 = 12 battery [package=battery]
  R2 = Resistor [tolerance=±5% resistance=15k package=THT]
  M1 = DC Motor  # not connected
  L1 = Solenoid
  L2 = Solenoid

nets:
  N1: Part1.A8, R14.pin_0, R16.Pin_1
  N2: Part1.A11, Mod1.S
  N3: Part1.A12, Mod2.S
  N4: Part1.A13, Mod3.S
  N5: Part1.A0, R3.Pin_1, R4.Pin_0
  N6: Part1.A1, R1.Pin_0, R2.Pin_0
  N7: Part1.A2, Part2.OUT
  N8: Part1.A4, R5.Pin_0, R6.Pin_1
  N9: Part1.A5, R7.Pin_0, R8.Pin_1
  N10: Part1.A7, R13.pin_0, R15.Pin_1
  N11: Part1.D21/SCL, Tiny_RTC1.SCL#1
  N12: Part1.D20/SDA, Tiny_RTC1.SDA#2
  N13: Part1.D15/RX3, U1.RXD
  N14: Part1.D14/TX3, U1.TXD
  GND: Part1.GND, U1.GND, R4.Pin_1, R5.Pin_1, R7.Pin_1, S1.Pin_3, S1.Pin_4, S2.Pin_3, S2.Pin_4, R9.Pin_1, R10.Pin_1, Tiny_RTC1.GND#4, Mod1.-, Mod2.-, Mod3.-, R12.pin_1, R13.pin_1, R14.pin_1, Part2.GND
  N15: Part1.D12_PWM, S2.Pin_1, S2.Pin_2
  N16: Part1.D11_PWM, S1.Pin_1, S1.Pin_2
  3V3: Part1.3V3, U1.VCC
  VIN: Part1.5V, R9.Pin_0, R10.Pin_0, Tiny_RTC1.VCC#3, Mod1.Vin, Mod2.Vin, Mod3.Vin, R11.Pin_0, R15.Pin_0, R16.Pin_0, Part2.5V
  N17: Part1.D48, LCD1.CS
  N18: Part1.D50/MISO, LCD1.SDO(MISO)
  N19: Part1.D51/MOSI, LCD1.SDI(MOSI)
  N20: Part1.D52/SCK, LCD1.SCK
  N21: Part1.D53/SS, LCD1.T_CS
  N22: KY-1.C, KY-2.C, KY-3.C, J6.pin2, BAT2.-, R2.Pin_1
  N23: KY-1.NO, J2.pin2, R3.Pin_0
  N24: KY-2.NO, J4.pin2, R8.Pin_0, L2.pin1
  N25: KY-3.NO, J3.pin2, R6.Pin_0, L1.pin1
  N26: KY-4.NC, J6.pin1
  N27: KY-4.C, F1.2, R1.Pin_1, D2.anode, D3.anode, BAT2.+
  N28: KY-4.NO, J5.pin2
  N29: F1.1, D1.anode
  N30: D1.cathode, J2.pin1
  N31: J3.pin1, D2.cathode, L1.pin2
  N32: J4.pin1, D3.cathode, L2.pin2
  N33: R11.Pin_1, R12.pin_0

custom parts:
  ESP8266 WiFi Module: Generic WiFi Module based on the ESP8266 with onboard PCB antenna and UART communications
  TONGLING Relay: The TONGLING 5V relay module is suitable for SCM development, home appliance control. It uses a 5V~12V TIL control signal which can control DC / AC signal.
  Tiny RTC: Tiny RTC I2C module DS1370Z RTC and AT24C32 EEPROM
  KY-015 Temperature & Humidity Sensor Module: KY-015 temperature and humidity sensor module, provides a low-latency serial interface to measure humidity and temperature.
  LCD_2.8_TFT_SPI_240X320_V1: LCD_2.8_TFT_SPI_240X320_V1 with sdcard and touch screen
  12 battery: 12V lead acid type battery, like the Husqvarna YTH2448 12V 35AH battery. This is the mini version 1/4 the size of the actual battery to be closer to typical breadboard parts (around 2in wide rathher than 7in). The pads in pcb are sized to accomidate up to 14ga wire (as these batterys will deliver high currents.)
