# Fritzing sketch שרטוט חשמלי סופי פרוייקט גמר (saved by Fritzing 0.9.4)
breadboards: 1

parts:
  part = Arduino Mega 2560 (Rev3)
  U1 = ESP8266 WiFi Module [part_number=ESP8266]
  Tiny_RTC1 = Tiny RTC
  Temp1 = KY-015 Temperature & Humidity Sensor Module [package="Breakout board"]
  Temp2 = KY-015 Temperature & Humidity Sensor Module [package="Breakout board"]
  Temp3 = KY-015 Temperature & Humidity Sensor Module [package="Breakout board"]
  KY-1 = TONGLING Relay [package=THT]
  KY-2 = TONGLING Relay [package=THT]
  KY-3 = TONGLING Relay [package=THT]
  KY-4 = TONGLING Relay [package=THT]
  BAT1 = 12 battery [package=battery]
  F1 = FUSE [package=fuse_5mm]
  R1 = Resistor [tolerance=±5% resistance=8.2k package="1206 [SMD]"]
  R2 = Resistor [tolerance=±5% resistance=15k package="1206 [SMD]"]
  D1 = Rectifier Diode [package="Melf DO-213 AA [SMD]"]
  Pump = DC Motor
  R3 = Resistor [tolerance=±5% resistance=8.2k package="1206 [SMD]"]
  R4 = Resistor [tolerance=±5% resistance=15k package="1206 [SMD]"]
  R5 = Resistor [tolerance=±5% resistance=8.2k package="1206 [SMD]"]
  R6 = Resistor [tolerance=±5% resistance=15k package="1206 [SMD]"]
  D2 = Rectifier Diode [package="Melf DO-213 AA [SMD]"]
  D3 = Rectifier Diode [package="Melf DO-213 AA [SMD]"]
  Normal_fosset = Solenoid
  Osmotic_fosset = Solenoid
  Spherical_faucet(Connector) = Screw terminal - 2 pins [package=THT]
  J2 = Screw terminal - 2 pins [package=THT]
  Part1 = Turbidity driver sensor
  S1 = SWITCH-MOMENTARY-2 [package=tactile_switch_tall]
  S2 = SWITCH-MOMENTARY-2 [package=tactile_switch_tall]
  R7 = Photocell (LDR) [package=THT]
  R8 = Photocell (LDR) [package=THT]
  R9 = Photocell (LDR) [package=THT]
  R10 = Resistor [tolerance=±5% resistance=10k package="1206 [SMD]"]
  R11 = Resistor [tolerance=±5% resistance=10k package="1206 [SMD]"]
  R12 = Resistor [tolerance=±5% resistance=10k package="1206 [SMD]"]
  R13 = Resistor [tolerance=±5% resistance=10k package="1206 [SMD]"]
  R14 = Resistor [tolerance=±5% resistance=10k package="1206 [SMD]"]
  LCD1 = LCD_2.8_TFT_SPI_240X320_V1 [package=2.8]
  R15 = Resistor [tolerance=±5% resistance=15k package="1206 [SMD]"]
  R16 = Resistor [tolerance=±5% resistance=21k package="1206 [SMD]"]

nets:
  N1: part.A8, R12.Pin_0
  N2: part.A11, Temp1.S
  N3: part.A12, Temp2.S
  N4: part.A13, Temp3.S
  N5: part.A0, R1.Pin_1, R2.Pin_0
  N6: part.A1, R15.Pin_0, R16.Pin_0
  N7: part.A2, Part1.OUT
  N8: part.A3, R11.Pin_0
  N9: part.A4, R3.Pin_1, R4.Pin_0
  N10: part.A5, R5.Pin_1
  N11: part.A7, R10.Pin_0
  N12: part.D15/RX3, U1.RXD
  N13: part.D14/TX3, U1.TXD
  N14: part.SCL, Tiny_RTC1.SCL
  N15: part.SDA, Tiny_RTC1.SDA
  GND: part.GND, U1.GND, Tiny_RTC1.GND, Temp1.-, Temp2.-, Temp3.-, KY-1.GND, KY-2.GND, KY-3.GND, KY-4.GND, R1.Pin_0, R3.Pin_0, R5.Pin_0, Part1.GND, S1.1, S2.1, R7.pin_0, R8.pin_0, R9.pin_0, R13.Pin_1, R14.Pin_1
  N16: part.D12_PWM, S2.2
  N17: part.D11_PWM, S1.2
  N18: part.D10_PWM, KY-4.IN
  N19: part.D9_PWM, KY-3.IN
  N20: part.D8_PWM, KY-2.IN
  3V3: part.3V3, U1.VCC
  VCC: part.5V, Tiny_RTC1.VCC, Temp1.Vin, Temp2.Vin, Temp3.Vin, KY-1.VCC, KY-2.VCC, KY-3.VCC, KY-4.VCC, Part1.5V, R10.Pin_1, R11.Pin_1, R12.Pin_1, R13.Pin_0, R14.Pin_0
  N21: part.D6_PWM, KY-1.IN
  N22: part.D48, LCD1.CS
  N23: part.D50, LCD1.SDO(MISO)
  N24: part.D51, LCD1.SDI(MOSI)
  N25: part.D52, LCD1.SCK
  N26: part.D53, LCD1.T_CS
  N27: KY-1.C, KY-2.C, KY-3.C, BAT1.-, J2.pin1, R15.Pin_1
  N28: KY-1.NO, R2.Pin_1, Pump.pin_2
  N29: KY-2.NO, R4.Pin_1, Normal_fosset.pin2
  N30: KY-3.NO, R6.Pin_1, Osmotic_fosset.pin2
  N31: KY-4.NC, Spherical_faucet(Connector).pin1
  N32: KY-4.C, BAT1.+, F1.1, D2.anode, D3.anode, R16.Pin_1
  N33: KY-4.NO, J2.pin2
  N34: F1.2, D1.anode
  N35: D1.cathode, Pump.pin_1
  N36: D2.cathode, Normal_fosset.pin1
  N37: D3.cathode, Osmotic_fosset.pin1

custom parts:
  ESP8266 WiFi Module: Generic WiFi Module based on the ESP8266 with onboard PCB antenna and UART communications
  Tiny RTC: Tiny RTC I2C module DS1370Z RTC and AT24C32 EEPROM
  KY-015 Temperature & Humidity Sensor Module: KY-015 temperature and humidity sensor module, provides a low-latency serial interface to measure humidity and temperature.
  TONGLING Relay: The TONGLING 5V relay module is suitable for SCM development, home appliance control. It uses a 5V~12V TIL control signal which can control DC / AC signal.
  12 battery: 12V lead acid type battery, like the Husqvarna YTH2448 12V 35AH battery. This is the mini version 1/4 the size of the actual battery to be closer to typical breadboard parts (around 2in wide rathher than 7in). The pads in pcb are sized to accomidate up to 14ga wire (as these batterys will deliver high currents.)
  LCD_2.8_TFT_SPI_240X320_V1: LCD_2.8_TFT_SPI_240X320_V1 with sdcard and touch screen
